// Logisim project control-logic.circ as structural Verilog: 4 circuits, main circuit control_logic
module control_logic (
  input  [31:0] inst,
  input  BrEq,
  input  BrLt,
  output PCSel,
  output out_5,
  output [2:0] ImmSel,
  output BrUn,
  output ASel,
  output BSel,
  output [3:0] ALUSel,
  output MemRW,
  output [1:0] WBSel,
  output CSRSel,
  output CSRWen
);

  wire add0, addi0, and0, and_9_out, and_10_out, and_11_out, and_12_out, and_13_out, and_14_out, and_15_out,
       and_19_out, and_20_out, and_21_out, and_22_out, and_23_out, andi0, AUIPC, Func3_0, Func3_1, Func3_2,
       Func3_3, Func3_4, Func3_5, Func3_6, Func3_7, Func7_0, Func7_1, Func7_20, JALR, LUI, not_1_out,
       not_2_out, not_3_out, not_4_out, not_5_out, not_6_out, not_7_out, not_8_out, not_9_out, not_10_out,
       or0, or_11_out, or_12_out, or_13_out, or_14_out, or_15_out, ori0, sll0, slli0, slt0, slti0, sra0,
       srai0, srl0, srli0, type_CSRW, type_I2, type_I13, type_L, type_R, type_S, type_SB, type_Ua, type_UJ,
       UPPER_0, UPPER_1, UPPER_2, UPPER_3, UPPER_4, xor0, xori0;
  wire [2:0] LOWER, multiplexer_8_out;
  wire [3:0] multiplexer_1_out, multiplexer_2_out, multiplexer_3_out, multiplexer_6_out, typeCSR, typeI,
       typeR;
  wire [5:3] RomInput;
  wire [15:0] rom_1_data;

  ROM #(.addrWidth(6), .dataWidth(16)) rom_1 (.addr({RomInput, LOWER}), .data(rom_1_data));
  Comparator #(.mode("unsigned"), .width(7)) comparator_1 (
    .a(inst[6:0]), .b(7'b0010011), .eq(type_I13));  // open: gt, lt
  Comparator #(.mode("unsigned"), .width(7)) comparator_2 (.a(inst[6:0]), .b(7'b0110011), .eq(type_R));  // open: gt, lt
  Comparator #(.mode("unsigned"), .width(7)) comparator_3 (.a(inst[6:0]), .b(7'b0000011), .eq(type_L));  // open: gt, lt
  Comparator #(.mode("unsigned"), .width(7)) comparator_4 (.a(inst[6:0]), .b(7'b1100111), .eq(JALR));  // open: gt, lt
  Comparator #(.mode("unsigned"), .width(7)) comparator_5 (.a(inst[6:0]), .b(7'b0100011), .eq(type_S));  // open: gt, lt
  Comparator #(.mode("unsigned"), .width(3)) comparator_6 (.a(inst[14:12]), .b(3'b000), .eq(Func3_0));  // open: gt, lt
  Comparator #(.mode("unsigned"), .width(3)) comparator_7 (.a(inst[14:12]), .b(3'b001), .eq(Func3_1));  // open: gt, lt
  Comparator #(.mode("unsigned"), .width(3)) comparator_8 (.a(inst[14:12]), .b(3'b010), .eq(Func3_2));  // open: gt, lt
  Comparator #(.mode("unsigned"), .width(3)) comparator_9 (.a(inst[14:12]), .b(3'b011), .eq(Func3_3));  // open: gt, lt
  Comparator #(.mode("unsigned"), .width(3)) comparator_10 (.a(inst[14:12]), .b(3'b100), .eq(Func3_4));  // open: gt, lt
  Comparator #(.mode("unsigned"), .width(3)) comparator_11 (.a(inst[14:12]), .b(3'b101), .eq(Func3_5));  // open: gt, lt
  Comparator #(.mode("unsigned"), .width(3)) comparator_12 (.a(inst[14:12]), .b(3'b110), .eq(Func3_6));  // open: gt, lt
  Comparator #(.mode("unsigned"), .width(3)) comparator_13 (.a(inst[14:12]), .b(3'b111), .eq(Func3_7));  // open: gt, lt
  and and_1 (addi0, type_I13, inst[12]);
  and and_2 (slli0, type_I13, inst[13]);
  and and_3 (slti0, type_I13, inst[14]);
  and and_4 (xori0, type_I13, Func3_3);
  Comparator #(.mode("unsigned"), .width(7)) comparator_14 (
    .a(inst[6:0]), .b(7'b1100011), .eq(type_SB));  // open: gt, lt
  Comparator #(.mode("unsigned"), .width(7)) comparator_15 (.a(inst[6:0]), .b(7'b0010111), .eq(AUIPC));  // open: gt, lt
  Comparator #(.mode("unsigned"), .width(7)) comparator_16 (.a(inst[6:0]), .b(7'b0110111), .eq(LUI));  // open: gt, lt
  Comparator #(.mode("unsigned"), .width(7)) comparator_17 (
    .a(inst[6:0]), .b(7'b1101111), .eq(type_UJ));  // open: gt, lt
  Comparator #(.mode("unsigned"), .width(7)) comparator_18 (
    .a(inst[6:0]), .b(7'b1110011), .eq(type_CSRW));  // open: gt, lt
  or or_1 (type_Ua, LUI, AUIPC);
  Comparator #(.mode("unsigned"), .width(7)) comparator_19 (
    .a(inst[31:25]), .b({7{1'b0}}), .eq(Func7_0));  // open: gt, lt
  Comparator #(.mode("unsigned"), .width(7)) comparator_20 (
    .a(inst[31:25]), .b(7'b0000001), .eq(Func7_1));  // open: gt, lt
  Comparator #(.mode("unsigned"), .width(7)) comparator_21 (
    .a(inst[31:25]), .b(7'b0100000), .eq(Func7_20));  // open: gt, lt
  and and_5 (srli0, type_I13, Func3_4);
  and and_6 (srai0, type_I13, Func3_5);
  and and_7 (ori0, type_I13, Func3_6);
  and and_8 (andi0, type_I13, Func3_7);
  or or_2 (type_I2, type_I13, type_L, JALR, type_CSRW);
  Multiplexer #(.enable("false"), .select(2), .width(4)) multiplexer_1 (
    .in0(4'b0000), .in1(4'b1000), .in2(4'b1100), .out(multiplexer_1_out), .sel({inst[30], inst[25]}));  // open: in3
  Multiplexer #(.enable("false"), .select(2), .width(4)) multiplexer_2 (
    .in0(4'b0101), .in2(4'b1101), .out(multiplexer_2_out), .sel({inst[30], inst[25]}));  // open: in1, in3
  Multiplexer #(.enable("false"), .select(2), .width(4)) multiplexer_3 (
    .in0(4'b0001), .in1(4'b1001), .out(multiplexer_3_out), .sel({inst[30], inst[25]}));  // open: in2, in3
  Multiplexer #(.enable("false"), .select(3), .width(4)) multiplexer_4 (
    .in0(multiplexer_1_out), .in1(multiplexer_3_out), .in2(4'b0010), .in3(4'b1011), .in4(4'b0100),
    .in5(multiplexer_2_out), .in6(4'b0110), .in7(4'b0111), .out(typeR), .sel(inst[14:12]));
  or or_3 (add0, type_R, inst[12]);
  or or_4 (sll0, type_R, inst[13]);
  or or_5 (slt0, type_R, inst[14]);
  or or_6 (xor0, type_R, Func3_3);
  Priority_Encoder priority_encoder_1 (
    .in0(1'b0), .in1(1'b0), .in2(1'b0), .in3(1'b0), .in4(1'b0), .in5(1'b0), .in6(1'b0), .in7(1'b0),
    .out(LOWER));  // open: en_in, gs, en_out
  Multiplexer #(.enable("false"), .select(5), .width(3)) multiplexer_5 (
    .in0(3'b000), .in4(3'b000), .in5(3'b011), .in8(3'b001), .in12(3'b000), .in13(3'b011), .in24(3'b010),
    .in25(3'b000), .in27(3'b100), .in28(multiplexer_8_out), .out(ImmSel), .sel(inst[6:2]));  // open: in1, in2, in3, in6, in7, in9, in10, in11, in14, in15, in16, in17, in18, in19, in20, in21, in22, in23, in26, in29, in30, in31
  Multiplexer #(.enable("false"), .select(2), .width(4)) multiplexer_6 (
    .in0(4'b0101), .in2(4'b1101), .out(multiplexer_6_out), .sel({inst[30], inst[25]}));  // open: in1, in3
  Multiplexer #(.enable("false"), .select(3), .width(4)) multiplexer_7 (
    .in0(4'b0000), .in1(4'b0001), .in2(4'b0010), .in4(4'b0100), .in5(multiplexer_6_out), .in6(4'b0110),
    .in7(4'b0111), .out(typeI), .sel(inst[14:12]));  // open: in3
  not not_1 (not_1_out, BrEq);
  not not_2 (not_2_out, inst[12]);
  not not_3 (not_3_out, BrLt);
  not not_4 (not_4_out, inst[12]);
  Multiplexer #(.enable("false"), .select(3), .width(3)) multiplexer_8 (
    .in1(3'b000), .in5(3'b101), .out(multiplexer_8_out), .sel(inst[14:12]));  // open: in0, in2, in3, in4, in6, in7
  or or_7 (srl0, type_R, Func3_4);
  or or_8 (sra0, type_R, Func3_5);
  or or_9 (or0, type_R, Func3_6);
  or or_10 (and0, type_R, Func3_7);
  Priority_Encoder priority_encoder_2 (
    .in0(UPPER_0), .in1(UPPER_1), .in2(UPPER_2), .in3(UPPER_3), .in4(UPPER_4), .in5(1'b0), .in6(1'b0),
    .in7(1'b0), .out(RomInput));  // open: en_in, gs, en_out
  Multiplexer #(.enable("false"), .select(3), .width(4)) multiplexer_9 (
    .in1(4'b0000), .in5(4'b1111), .out(typeCSR), .sel(inst[14:12]));  // open: in0, in2, in3, in4, in6, in7
  and and_9 (and_9_out, inst[12], not_1_out);
  and and_10 (and_10_out, not_2_out, BrEq);
  and and_11 (and_11_out, inst[12], not_3_out);
  and and_12 (and_12_out, not_4_out, BrLt);
  not not_5 (not_5_out, inst[14]);
  or or_11 (or_11_out, and_9_out, and_10_out);
  or or_12 (or_12_out, and_11_out, and_12_out);
  Multiplexer #(.enable("false"), .select(5), .width(2)) multiplexer_10 (
    .in0(2'b10), .in4(2'b01), .in5(2'b01), .in8(2'b11), .in12(2'b01), .in13(2'b01), .in24(2'b11),
    .in25(2'b00), .in27(2'b00), .in28(2'b11), .out(WBSel), .sel(inst[6:2]));  // open: in1, in2, in3, in6, in7, in9, in10, in11, in14, in15, in16, in17, in18, in19, in20, in21, in22, in23, in26, in29, in30, in31
  and and_13 (and_13_out, not_5_out, or_11_out);
  and and_14 (and_14_out, inst[14], or_12_out);
  regwen_helper regwen_helper_1 (.in_1(inst[6:0]), .out_2(out_5));
  bsel_helper bsel_helper_1 (.in_1(inst[6:0]), .out_2(BSel));
  Multiplexer #(.enable("false"), .select(5), .width(4)) multiplexer_11 (
    .in0(4'b0000), .in4(typeI), .in5(4'b0000), .in8(4'b0000), .in12(typeR), .in13(4'b1111), .in24(4'b0000),
    .in25(4'b0000), .in27(4'b0000), .in28(typeCSR), .out(ALUSel), .sel(inst[6:2]));  // open: in1, in2, in3, in6, in7, in9, in10, in11, in14, in15, in16, in17, in18, in19, in20, in21, in22, in23, in26, in29, in30, in31
  or or_13 (or_13_out, inst[2], and_13_out);
  not not_6 (not_6_out, inst[4]);
  or or_14 (or_14_out, or_13_out, and_14_out);
  and and_15 (and_15_out, inst[6], not_6_out);
  and and_16 (PCSel, or_14_out, and_15_out);
  Multiplexer #(.enable("false"), .select(5)) multiplexer_12 (
    .in0(1'b1), .in4(1'b1), .in5(1'b0), .in8(1'b1), .in12(1'b1), .in13(1'b0), .in24(1'b0), .in25(1'b1),
    .in27(1'b0), .in28(1'b0), .out(ASel), .sel(inst[6:2]));  // open: in1, in2, in3, in6, in7, in9, in10, in11, in14, in15, in16, in17, in18, in19, in20, in21, in22, in23, in26, in29, in30, in31
  not not_7 (not_7_out, inst[2]);
  not not_8 (not_8_out, inst[3]);
  memRW_helper memrw_helper_1 (.in_1(inst[6:0]), .out_2(MemRW));
  and and_17 (CSRWen, not_7_out, not_8_out, inst[4], inst[5], inst[6]);
  not not_9 (not_9_out, inst[13]);
  not not_10 (not_10_out, inst[12]);
  or or_15 (or_15_out, inst[13], inst[14]);
  and and_18 (UPPER_0, type_R, not_9_out);
  and and_19 (and_19_out, type_R, inst[13]);
  and and_20 (and_20_out, inst[12], type_I13);
  and and_21 (and_21_out, type_S, inst[12]);
  and and_22 (and_22_out, not_10_out, type_I13);
  and and_23 (and_23_out, or_15_out, type_S);
  or or_16 (UPPER_3, and_23_out, type_SB);
  or or_17 (UPPER_4, JALR, AUIPC, type_UJ, LUI, type_CSRW);
  or or_18 (UPPER_1, and_19_out, type_L, and_20_out);
  or or_19 (UPPER_2, and_21_out, and_22_out);

  assign BrUn = inst[13];

  // Other names for the same wires on the sheet: func3[2:0] = inst[14:12]; func3_1_t = inst[13]; RegWEn = out_5;
  //   opcode[6:0] = inst[6:0]; MUX_opcode[4:0] = inst[6:2]; opcode2 = inst[2]; opcode3 = inst[3]; opcode4 = inst[4];
  //   opcode5 = inst[5]; opcode6 = inst[6]; func3_0_t = inst[12]; func3_2_t = inst[14]; func7[6:0] = inst[31:25];
  //   func7_2 = inst[26]; func7_3 = inst[27]; func7_4 = inst[28]; func7_5 = inst[29]; func7_7 = inst[31];
  //   RomInput[2:0] = LOWER; UPPER[2:0] = RomInput; func7_1_t = inst[25]; twobit_7[1:0] = {inst[30], inst[25]};
  //   func7_6 = inst[30]

  // Notes on the sheet:
  //   Connect ROM Input here ->
  //   INPUTS to your circuit
  //   contents of rom_1 (hex, n*v repeats v):
  //   8004 8104 8184 8024 8124 8964 8044 8084 80a4 81a4 80c4 80e4 9208 9208 9208 9204 9224 9244 9284 92a4
  //   93a4 92c4 92e4 2210 2210 2210 4*3600 3e00 3e00 c604 c3e4 d600 9200 1 6003
  //   ROM FOR CONTROL LOGIC
  //   CLOSE
  //   WIRE
  //   TO
  //   USE
  //   ROM
  //   DON'T CHANGE THE LOCATIONS OF THE INPUTS AND OUTPUTS!
  //   OUTPUT from your circuit
  //   Reminder: Use combinational logic for PCSel
endmodule

module regwen_helper (
  input  [6:0] in_1,
  output out_2
);

  wire not_1_out, or_1_out;

  or or_1 (or_1_out, in_1[2], in_1[3], in_1[4]);
  not not_1 (not_1_out, in_1[5]);
  or or_2 (out_2, or_1_out, not_1_out);

  // Other names for the same wires on the sheet: func7_2 = in_1[2]; func_7[5:1] = in_1[6:2]; func7_3 = in_1[3];
  //   func7_4 = in_1[4]; func7_5 = in_1[5]; func7_6 = in_1[6]
endmodule

module bsel_helper (
  input  [6:0] in_1,
  output out_2
);

  wire not_1_out, not_2_out, or_1_out, or_2_out;

  or or_1 (or_1_out, in_1[6], in_1[2], in_1[3]);
  not not_1 (not_1_out, in_1[4]);
  not not_2 (not_2_out, in_1[5]);
  or or_2 (or_2_out, not_1_out, not_2_out);
  or or_3 (out_2, or_1_out, or_2_out);

  // Other names for the same wires on the sheet: func7_2 = in_1[2]; func7_3 = in_1[3]; func7_4 = in_1[4];
  //   func7_5 = in_1[5]; func7_6 = in_1[6]
endmodule

module memRW_helper (
  input  [6:0] in_1,
  output out_2
);

  wire nand_1_out, not_1_out;

  not not_1 (not_1_out, in_1[6]);
  nand nand_1 (nand_1_out, in_1[2], in_1[3], in_1[4]);
  and and_1 (out_2, nand_1_out, in_1[5], not_1_out);

  // Other names for the same wires on the sheet: func7_2 = in_1[2]; func7_3 = in_1[3]; func7_4 = in_1[4];
  //   func7_5 = in_1[5]; func7_6 = in_1[6]
endmodule
