// Logisim project cpu.circ as structural Verilog: 1 circuit, main circuit cpu
module cpu (
  input  clk,
  input  [31:0] INSTRUCTION,
  input  [31:0] MEM_READ_DATA,
  output [31:0] MEM_WRITE_ADDRESS,
  output [31:0] PROGRAM_COUNTER,
  output [31:0] ra,
  output [31:0] sp,
  output [31:0] t0,
  output [31:0] t1,
  output [31:0] t2,
  output [31:0] s0,
  output [31:0] s1,
  output [31:0] a0,
  output [31:0] tohost,
  output [3:0] MEM_WRITE_ENABLE,
  output [31:0] MEM_WRITE_DATA
);

  wire ASel, bit2, bit3, bit4, bit5, bit6, BrEq, BrLt, BrUn, BSel, CSRWen, func3_bit0, func3_bit1,
       func3_bit2, MemRW, PCSel, RegWEn;
  wire [1:0] opcode_1, WBSel;
  wire [2:0] ImmSel;
  wire [3:0] ALUSel, mask, multiplexer_6_out, multiplexer_7_out;
  wire [6:0] funct7;
  wire [24:7] Pipe_INST;
  wire [31:0] adder_2_out, bit_extender_1_out, bit_extender_2_out, bit_extender_3_out, bit_extender_4_out,
       bit_extender_5_out, bit_extender_6_out, bit_extender_7_out, CSR_din, imm, multiplexer_1_out,
       multiplexer_2_out, multiplexer_10_out, multiplexer_11_out, multiplexer_13_out, multiplexer_14_out,
       PC4, Pipe_PC, read_A, read_B, Read_Data, rs_data1, rs_data2, Write_Data_WB;

  Adder #(.width(32)) adder_1 (.a(PROGRAM_COUNTER), .b(32'h4), .out(PC4));  // open: cin, cout
  Multiplexer #(.enable("false"), .width(32)) multiplexer_1 (
    .in0(PC4), .in1(MEM_WRITE_ADDRESS), .out(multiplexer_1_out), .sel(PCSel));
  Register #(.width(32)) PC (.D(multiplexer_1_out), .clk(clk), .Q(PROGRAM_COUNTER));  // open: en, clr
  Multiplexer #(.enable("false"), .width(32)) multiplexer_2 (
    .in0(INSTRUCTION), .in1(32'h13), .out(multiplexer_2_out), .sel(PCSel));
  Register #(.width(32)) register_1 (
    .D(multiplexer_2_out), .clk(clk),
    .Q({funct7, Pipe_INST[24:15], func3_bit2, func3_bit1, func3_bit0, Pipe_INST[11:7], bit6, bit5, bit4, bit3, bit2, opcode_1}));  // open: en, clr
  Register #(.width(32)) register_2 (.D(PROGRAM_COUNTER), .clk(clk), .Q(Pipe_PC));  // open: en, clr
  control_logic control_logic_1 (
    .CSRWen(CSRWen), .PCSel(PCSel), .out_5(RegWEn), .ImmSel(ImmSel), .BrUn(BrUn), .ASel(ASel), .BSel(BSel),
    .ALUSel(ALUSel), .MemRW(MemRW), .WBSel(WBSel),
    .inst({funct7, Pipe_INST[24:15], func3_bit2, func3_bit1, func3_bit0, Pipe_INST[11:7], bit6, bit5, bit4, bit3, bit2, opcode_1}),
    .BrEq(BrEq), .BrLt(BrLt));  // open: CSRSel
  regfile regfile_1 (
    .rs1(Pipe_INST[19:15]), .rs2(Pipe_INST[24:20]), .rd(Pipe_INST[11:7]), .Write_Data(Write_Data_WB),
    .RegWEn(RegWEn), .clk(clk), .ra(ra), .sp(sp), .t0(t0), .t1(t1), .t2(t2), .s0(s0), .s1(s1), .a0(a0),
    .Read_Data_1(rs_data1), .Read_Data_2(rs_data2));
  imm_gen imm_gen_1 (
    .inst({funct7, Pipe_INST[24:15], func3_bit2, func3_bit1, func3_bit0, Pipe_INST[11:7], bit6, bit5, bit4, bit3, bit2, opcode_1}),
    .ImmSel(ImmSel), .imm(imm));
  branch_comp branch_comp_1 (.rs1(rs_data1), .rs2(rs_data2), .BrUn(BrUn), .BrEq(BrEq), .BrLt(BrLt));
  Multiplexer #(.enable("false"), .select(3), .width(32)) multiplexer_3 (
    .in1(rs_data1), .in5(imm), .out(CSR_din), .sel({func3_bit2, func3_bit1, func3_bit0}));  // open: in0, in2, in3, in4, in6, in7
  Multiplexer #(.enable("false"), .width(32)) multiplexer_4 (.in0(Pipe_PC), .in1(rs_data1), .out(read_A), .sel(ASel));
  Multiplexer #(.enable("false"), .width(32)) multiplexer_5 (.in0(rs_data2), .in1(imm), .out(read_B), .sel(BSel));
  // csr csr_1: pin names not known; wires that end beside it: {funct7, Pipe_INST[24:20]}, CSR_din, CSRWen, clk, tohost
  alu alu_1 (.Result(MEM_WRITE_ADDRESS), .A(read_A), .B(read_B), .ALUSel(ALUSel));
  Adder #(.width(32)) adder_2 (.a(Pipe_PC), .b(32'h4), .out(adder_2_out));  // open: cin, cout
  Multiplexer #(.enable("false"), .select(2), .width(4)) multiplexer_6 (
    .in0(4'b0001), .in1(4'b0010), .in2(4'b0100), .in3(4'b1000), .out(multiplexer_6_out),
    .sel(MEM_WRITE_ADDRESS[1:0]));
  Multiplexer #(.enable("false"), .select(2), .width(4)) multiplexer_7 (
    .in0(4'b0011), .in1(4'b0110), .in2(4'b1100), .out(multiplexer_7_out), .sel(MEM_WRITE_ADDRESS[1:0]));  // open: in3
  Multiplexer #(.enable("false"), .select(2), .width(32)) multiplexer_8 (
    .in0(adder_2_out), .in1(MEM_WRITE_ADDRESS), .in2(Read_Data), .out(Write_Data_WB), .sel(WBSel));  // open: in3
  Multiplexer #(.enable("false"), .select(3), .width(4)) multiplexer_9 (
    .in0(multiplexer_6_out), .in1(multiplexer_7_out), .in2(4'b1111), .out(mask),
    .sel({func3_bit2, func3_bit1, func3_bit0}));  // open: in3, in4, in5, in6, in7
  assign bit_extender_1_out = {{24{MEM_READ_DATA[7]}}, MEM_READ_DATA[7:0]};  // Bit_Extender bit_extender_1
  assign bit_extender_2_out = {{24{MEM_READ_DATA[15]}}, MEM_READ_DATA[15:8]};  // Bit_Extender bit_extender_2
  assign bit_extender_3_out = {{24{MEM_READ_DATA[23]}}, MEM_READ_DATA[23:16]};  // Bit_Extender bit_extender_3
  assign bit_extender_4_out = {{24{MEM_READ_DATA[31]}}, MEM_READ_DATA[31:24]};  // Bit_Extender bit_extender_4
  assign bit_extender_5_out = {{16{MEM_READ_DATA[15]}}, MEM_READ_DATA[15:0]};  // Bit_Extender bit_extender_5
  assign bit_extender_6_out = {{16{MEM_READ_DATA[31]}}, MEM_READ_DATA[31:16]};  // Bit_Extender bit_extender_6
  assign bit_extender_7_out = {{24{1'b0}}, rs_data2[7:0]};  // Bit_Extender bit_extender_7
  Multiplexer #(.enable("false"), .select(2), .width(32)) multiplexer_10 (
    .in0(bit_extender_1_out), .in1(bit_extender_2_out), .in2(bit_extender_3_out), .in3(bit_extender_4_out),
    .out(multiplexer_10_out), .sel(MEM_WRITE_ADDRESS[1:0]));
  Multiplexer #(.enable("false"), .select(2), .width(32)) multiplexer_11 (
    .in0(bit_extender_5_out), .in2(bit_extender_6_out), .out(multiplexer_11_out), .sel(MEM_WRITE_ADDRESS[1:0]));  // open: in1, in3
  Multiplexer #(.enable("false"), .width(4)) multiplexer_12 (
    .in0(4'b0000), .in1(mask), .out(MEM_WRITE_ENABLE), .sel(MemRW));
  Multiplexer #(.enable("false"), .select(2), .width(32)) multiplexer_13 (
    .in0(bit_extender_7_out), .in1({{16{1'b0}}, rs_data2[7:0], {8{1'b0}}}),
    .in2({{8{1'b0}}, rs_data2[7:0], {16{1'b0}}}), .in3({rs_data2[7:0], {24{1'b0}}}),
    .out(multiplexer_13_out), .sel(MEM_WRITE_ADDRESS[1:0]));
  Multiplexer #(.enable("false"), .select(2), .width(32)) multiplexer_14 (
    .in0({{16{1'b0}}, rs_data2[15:0]}), .in2({rs_data2[15:0], {16{1'b0}}}), .out(multiplexer_14_out),
    .sel(MEM_WRITE_ADDRESS[1:0]));  // open: in1, in3
  Multiplexer #(.enable("false"), .select(3), .width(32)) multiplexer_15 (
    .in0(multiplexer_10_out), .in1(multiplexer_11_out), .in2(MEM_READ_DATA), .out(Read_Data),
    .sel({func3_bit2, func3_bit1, func3_bit0}));  // open: in3, in4, in5, in6, in7
  Multiplexer #(.enable("false"), .select(3), .width(32)) multiplexer_16 (
    .in0(multiplexer_13_out), .in1(multiplexer_14_out), .in2(rs_data2), .out(MEM_WRITE_DATA),
    .sel({func3_bit2, func3_bit1, func3_bit0}));  // open: in3, in4, in5, in6, in7

  // Other names for the same wires on the sheet: ALU_OUT[31:0] = MEM_WRITE_ADDRESS;
  //   last_bit2[1:0] = MEM_WRITE_ADDRESS[1:0];
  //   Pipe_INST (some bits) = {funct7, func3_bit2, func3_bit1, func3_bit0, bit6, bit5, bit4, bit3, bit2, opcode_1};
  //   opcode_1[6:2] = {bit6, bit5, bit4, bit3, bit2}; rd[4:0] = Pipe_INST[11:7];
  //   funct3[2:0] = {func3_bit2, func3_bit1, func3_bit0}; rs1[4:0] = Pipe_INST[19:15]; rs2[4:0] = Pipe_INST[24:20]

  // Notes on the sheet:
  //   Output to IMEM
  //   IMEM (do **NOT** move this)
  //   Inputs from IMEM
  //   Inputs/Outputs for testing. Do **NOT** move these.
  //   It is OK to move the PC, RegFile, ALU, MEM, Branch Comp, Imm Gen, and Control Logic to wherever is most convenient for you when constructing your CPU, and to delete this text
  //   Outputs To DMEM
  //   DMEM (do **NOT** move this)
  //   Inputs From DMEM
endmodule
