// Logisim project regfile.circ as structural Verilog: 1 circuit, main circuit regfile
module regfile (
  input  [4:0] rs1,
  input  [4:0] rs2,
  input  [4:0] rd,
  input  [31:0] Write_Data,
  input  RegWEn,
  input  clk,
  output [31:0] ra,
  output [31:0] sp,
  output [31:0] t0,
  output [31:0] t1,
  output [31:0] t2,
  output [31:0] s0,
  output [31:0] s1,
  output [31:0] a0,
  output [31:0] Read_Data_1,
  output [31:0] Read_Data_2
);

  wire Q1, Q2, Q3, Q4, Q5, Q6, Q7, Q8, Q9, Q10, Q11, Q12, Q13, Q14, Q15, Q16, Q17, Q18, Q19, Q20, Q21, Q22,
       Q23, Q24, Q25, Q26, Q27, Q28, Q29, Q30, Q31;
  wire [31:0] x3, x4, x11, x12, x13, x14, x15, x16, x17, x18, x19, x20, x21, x22, x23, x24, x25, x26, x27,
       x28, x29, x30, x31;

  Register #(.width(32)) register_1 (.D(Write_Data), .en(Q1), .clk(clk), .Q(ra));  // open: clr
  Register #(.width(32)) register_2 (.D(Write_Data), .en(Q5), .clk(clk), .Q(t0));  // open: clr
  Register #(.width(32)) register_3 (.D(Write_Data), .en(Q9), .clk(clk), .Q(s1));  // open: clr
  Register #(.width(32)) register_4 (.D(Write_Data), .en(Q13), .clk(clk), .Q(x13));  // open: clr
  Register #(.width(32)) register_5 (.D(Write_Data), .en(Q17), .clk(clk), .Q(x17));  // open: clr
  Register #(.width(32)) register_6 (.D(Write_Data), .en(Q21), .clk(clk), .Q(x21));  // open: clr
  Register #(.width(32)) register_7 (.D(Write_Data), .en(Q25), .clk(clk), .Q(x25));  // open: clr
  Register #(.width(32)) register_8 (.D(Write_Data), .en(Q29), .clk(clk), .Q(x29));  // open: clr
  Register #(.width(32)) register_9 (.D(Write_Data), .en(Q6), .clk(clk), .Q(t1));  // open: clr
  Register #(.width(32)) register_10 (.D(Write_Data), .en(Q14), .clk(clk), .Q(x14));  // open: clr
  Register #(.width(32)) register_11 (.D(Write_Data), .en(Q18), .clk(clk), .Q(x18));  // open: clr
  Register #(.width(32)) register_12 (.D(Write_Data), .en(Q22), .clk(clk), .Q(x22));  // open: clr
  Register #(.width(32)) register_13 (.D(Write_Data), .en(Q26), .clk(clk), .Q(x26));  // open: clr
  Register #(.width(32)) register_14 (.D(Write_Data), .en(Q30), .clk(clk), .Q(x30));  // open: clr
  Register #(.width(32)) register_15 (.D(Write_Data), .en(Q2), .clk(clk), .Q(sp));  // open: clr
  Register #(.width(32)) register_16 (.D(Write_Data), .en(Q10), .clk(clk), .Q(a0));  // open: clr
  Demultiplexer #(.enable("false"), .select(5)) demultiplexer_1 (
    .out1(Q1), .out2(Q2), .out3(Q3), .out4(Q4), .out5(Q5), .out6(Q6), .out7(Q7), .out8(Q8), .out9(Q9),
    .out10(Q10), .out11(Q11), .out12(Q12), .out13(Q13), .out14(Q14), .out15(Q15), .out16(Q16), .out17(Q17),
    .out18(Q18), .out19(Q19), .out20(Q20), .out21(Q21), .out22(Q22), .out23(Q23), .out24(Q24), .out25(Q25),
    .out26(Q26), .out27(Q27), .out28(Q28), .out29(Q29), .out30(Q30), .out31(Q31), .in(RegWEn), .sel(rd));  // open: out0
  Register #(.width(32)) register_17 (.D(Write_Data), .en(Q27), .clk(clk), .Q(x27));  // open: clr
  Multiplexer #(.enable("false"), .select(5), .width(32)) multiplexer_1 (
    .in0({32{1'b0}}), .in1(ra), .in2(sp), .in3(x3), .in4(x4), .in5(t0), .in6(t1), .in7(t2), .in8(s0),
    .in9(s1), .in10(a0), .in11(x11), .in12(x12), .in13(x13), .in14(x14), .in15(x15), .in16(x16), .in17(x17),
    .in18(x18), .in19(x19), .in20(x20), .in21(x21), .in22(x22), .in23(x23), .in24(x24), .in25(x25),
    .in26(x26), .in27(x27), .in28(x28), .in29(x29), .in30(x30), .in31(x31), .out(Read_Data_1), .sel(rs1));
  Register #(.width(32)) register_18 (.D(Write_Data), .en(Q3), .clk(clk), .Q(x3));  // open: clr
  Register #(.width(32)) register_19 (.D(Write_Data), .en(Q7), .clk(clk), .Q(t2));  // open: clr
  Register #(.width(32)) register_20 (.D(Write_Data), .en(Q11), .clk(clk), .Q(x11));  // open: clr
  Register #(.width(32)) register_21 (.D(Write_Data), .en(Q15), .clk(clk), .Q(x15));  // open: clr
  Register #(.width(32)) register_22 (.D(Write_Data), .en(Q19), .clk(clk), .Q(x19));  // open: clr
  Register #(.width(32)) register_23 (.D(Write_Data), .en(Q23), .clk(clk), .Q(x23));  // open: clr
  Register #(.width(32)) register_24 (.D(Write_Data), .en(Q31), .clk(clk), .Q(x31));  // open: clr
  Register #(.width(32)) register_25 (.D(Write_Data), .en(Q4), .clk(clk), .Q(x4));  // open: clr
  Register #(.width(32)) register_26 (.D(Write_Data), .en(Q8), .clk(clk), .Q(s0));  // open: clr
  Register #(.width(32)) register_27 (.D(Write_Data), .en(Q12), .clk(clk), .Q(x12));  // open: clr
  Register #(.width(32)) register_28 (.D(Write_Data), .en(Q16), .clk(clk), .Q(x16));  // open: clr
  Register #(.width(32)) register_29 (.D(Write_Data), .en(Q20), .clk(clk), .Q(x20));  // open: clr
  Register #(.width(32)) register_30 (.D(Write_Data), .en(Q24), .clk(clk), .Q(x24));  // open: clr
  Register #(.width(32)) register_31 (.D(Write_Data), .en(Q28), .clk(clk), .Q(x28));  // open: clr
  Multiplexer #(.enable("false"), .select(5), .width(32)) multiplexer_2 (
    .in0({32{1'b0}}), .in1(ra), .in2(sp), .in3(x3), .in4(x4), .in5(t0), .in6(t1), .in7(t2), .in8(s0),
    .in9(s1), .in10(a0), .in11(x11), .in12(x12), .in13(x13), .in14(x14), .in15(x15), .in16(x16), .in17(x17),
    .in18(x18), .in19(x19), .in20(x20), .in21(x21), .in22(x22), .in23(x23), .in24(x24), .in25(x25),
    .in26(x26), .in27(x27), .in28(x28), .in29(x29), .in30(x30), .in31(x31), .out(Read_Data_2), .sel(rs2));

  // Other names for the same wires on the sheet: read_data1[31:0] = Read_Data_1; read_data2[31:0] = Read_Data_2;
  //   read_reg1[4:0] = rs1; read_reg2[4:0] = rs2; write_en = RegWEn; write_reg[4:0] = rd; x1[31:0] = ra;
  //   x2[31:0] = sp; x5[31:0] = t0; x6[31:0] = t1; x7[31:0] = t2; x8[31:0] = s0; x9[31:0] = s1; x10[31:0] = a0

  // Notes on the sheet:
  //   INPUTS to your circuit
  //   DON'T CHANGE THE LOCATIONS OF THE INPUTS AND OUTPUTS!
  //   These are DEBUG/TEST outputs from your circuit.
  //   OUTPUTS from your circuit
endmodule
